# Fritzing sketch arduinochess (saved by Fritzing 0.9.3b)

parts:
  Part1 = Arduino Mega 2560 (Rev3)
  Part2 = 2.4 Touchscreen TFT Breakout w:MicroSD
  Part3 = Thumb Joystick
  Part4 = Thumb Joystick

nets:
  N1: Part1.A0, Part3.VERT
  N2: Part1.A1, Part3.HORZ
  N3: Part1.A2, Part2.Y+
  N4: Part1.A3, Part2.X-
  N5: Part1.A4, Part4.VERT
  N6: Part1.A5, Part4.HORZ
  N7: Part1.D10_PWM, Part2.CS
  N8: Part1.D9_PWM, Part2.WR_DC
  N9: Part1.D8_PWM, Part4.SEL
  VCC: Part1.5V, Part2.VIN, Part3.VCC, Part4.VCC
  GND: Part1.GND, Part2.GND, Part3.GND, Part4.GND
  N10: Part1.D2_PWM, Part3.SEL
  N11: Part1.D4_PWM, Part2.X+
  N12: Part1.D5_PWM, Part2.Y-
  N13: Part1.D6_PWM, Part2.SD_CS
  N14: Part1.D50, Part2.MISO
  N15: Part1.D51, Part2.MOSI
  N16: Part1.D52, Part2.CLK

custom parts:
  2.4 Touchscreen TFT Breakout w:MicroSD: Add some jazz & pizzazz to your project with a color touchscreen LCD. This TFT display is 2.4" diagonal with a bright (4 white-LED) backlight and it's colorful! 240x320 pixels with individual RGB pixel control, this has way more resolution than a black and white 128x64 display. As a bonus, this display has a resistive touchscreen attached to it already, so you can detect finger presses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
